// Logisim project part1.circ as structural Verilog: 3 circuits, main circuit 4bitcounter
module _4bitcounter (
  input  clk,
  input  inc,
  input  rst,
  output [3:0] \output 
);

  wire and_1_out, and_2_out, and_3_out, and_4_out, and_5_out, and_6_out, and_7_out, not_1_out, xor_1_out,
       xor_2_out, xor_3_out, xor_4_out;

  not not_1 (not_1_out, rst);
  xor xor_1 (xor_1_out, \output [0], inc);
  and and_1 (and_1_out, \output [0], inc);
  xor xor_2 (xor_2_out, and_1_out, \output [1]);
  and and_2 (and_2_out, \output [0], \output [1], inc);
  xor xor_3 (xor_3_out, and_2_out, \output [2]);
  and and_3 (and_3_out, \output [0], \output [1], \output [2], inc);
  xor xor_4 (xor_4_out, and_3_out, \output [3]);
  and and_4 (and_4_out, xor_1_out, not_1_out);
  and and_5 (and_5_out, xor_2_out, not_1_out);
  and and_6 (and_6_out, xor_3_out, not_1_out);
  and and_7 (and_7_out, xor_4_out, not_1_out);
  D_Flip_Flop d_ff_1 (.clk(clk), .D(and_4_out), .Q(\output [0]));  // open: Qn, preset, en, reset
  D_Flip_Flop d_ff_2 (.clk(clk), .D(and_5_out), .Q(\output [1]));  // open: Qn, preset, en, reset
  D_Flip_Flop d_ff_3 (.clk(clk), .D(and_6_out), .Q(\output [2]));  // open: Qn, preset, en, reset
  D_Flip_Flop d_ff_4 (.clk(clk), .D(and_7_out), .Q(\output [3]));  // open: Qn, preset, en, reset
endmodule

// register
module _16_bit_register (
  input  [15:0] in_1,
  input  clk,
  input  load,
  input  inc,
  input  clr
);

  wire and_1_out, and_2_out, and_3_out, and_4_out, b0_q, b1_q, b2_q, b3_q, xor_1_out, xor_2_out, xor_3_out,
       xor_4_out;

  xor xor_1 (xor_1_out, in_1[0], b0_q);
  and and_1 (and_1_out, xor_1_out, load);
  xor xor_2 (xor_2_out, in_1[1], b1_q);
  and and_2 (and_2_out, xor_2_out, load);
  xor xor_3 (xor_3_out, in_1[2], b2_q);
  and and_3 (and_3_out, xor_3_out, load);
  xor xor_4 (xor_4_out, in_1[3], b3_q);
  and and_4 (and_4_out, xor_4_out, load);
  J_K_Flip_Flop b0 (.J(and_1_out), .clk(clk), .K(clr), .Q(b0_q));  // open: Qn, preset, en, reset
  J_K_Flip_Flop b1 (.J(and_2_out), .clk(clk), .K(clr), .Q(b1_q));  // open: Qn, preset, en, reset
  J_K_Flip_Flop b2 (.J(and_3_out), .clk(clk), .K(clr), .Q(b2_q));  // open: Qn, preset, en, reset
  J_K_Flip_Flop b3 (.J(and_4_out), .clk(clk), .K(clr), .Q(b3_q));  // open: Qn, preset, en, reset
  J_K_Flip_Flop b4 (.clk(clk), .K(clr));  // open: J, Q, Qn, preset, en, reset
  J_K_Flip_Flop b5 (.clk(clk), .K(clr));  // open: J, Q, Qn, preset, en, reset
  J_K_Flip_Flop b6 (.clk(clk), .K(clr));  // open: J, Q, Qn, preset, en, reset
  J_K_Flip_Flop b7 (.clk(clk), .K(clr));  // open: J, Q, Qn, preset, en, reset
  J_K_Flip_Flop b8 (.clk(clk), .K(clr));  // open: J, Q, Qn, preset, en, reset
  J_K_Flip_Flop b9 (.clk(clk), .K(clr));  // open: J, Q, Qn, preset, en, reset
  J_K_Flip_Flop b10 (.clk(clk), .K(clr));  // open: J, Q, Qn, preset, en, reset
  J_K_Flip_Flop b11 (.clk(clk), .K(clr));  // open: J, Q, Qn, preset, en, reset
  J_K_Flip_Flop b12 (.clk(clk), .K(clr));  // open: J, Q, Qn, preset, en, reset
  J_K_Flip_Flop b13 (.clk(clk), .K(clr));  // open: J, Q, Qn, preset, en, reset
  J_K_Flip_Flop b14 (.clk(clk), .K(clr));  // open: J, Q, Qn, preset, en, reset
  J_K_Flip_Flop b15 (.clk(clk), .K(clr));  // open: J, Q, Qn, preset, en, reset
endmodule

module main (
);

  wire clock_1_out, load_out, rst_out;
  wire [3:0] n4bitcounter_1_output;

  Button rst (.out(rst_out));
  Button load (.out(load_out));
  Clock clock_1 (.out(clock_1_out));
  Hex_Digit_Display hex_digit_display_1 (.value(n4bitcounter_1_output));  // open: dp
  _4bitcounter u_4bitcounter_1 (.clk(clock_1_out), .inc(1'b1), .rst(rst_out), .\output (n4bitcounter_1_output));
  _16_bit_register u_16_bit_register_1 (.in_1(16'hf312), .clk(clock_1_out), .load(load_out), .inc(1'b0), .clr(rst_out));
endmodule
